// Logisim project FOUR_BIT_ALU.circ as structural Verilog: 1 circuit, main circuit main
module main (
  input  [3:0] A,
  input  [3:0] B,
  input  S2,
  input  S1,
  input  S0,
  output Cout,
  output [3:0] OUTPUT
);

  wire adder_1_cout, adder_2_cout, adder_3_cout, adder_4_cout, not_1_out, OR1_out, OR2_out, OR3_out,
       XOR1_out, XOR2_out, XOR3_out, XOR4_out, XOR_2_out;
  wire [3:0] adder_1_out, AND_out, OR_out, XOR_out;

  xor XOR1 (XOR1_out, B[0], S0);
  xor XOR2 (XOR2_out, B[1], S0);
  xor XOR3 (XOR3_out, B[2], S0);
  xor XOR4 (XOR4_out, B[3], S0);
  assign AND_out = A & B;  // AND_Gate AND, 4 bits wide
  assign OR_out = A | B;  // OR_Gate OR, 4 bits wide
  assign XOR_out = A ^ B;  // XOR_Gate XOR, 4 bits wide
  Adder #(.width(1)) adder_1 (.a(XOR1_out), .b(A[0]), .out(adder_1_out[0]), .cin(S0), .cout(adder_1_cout));
  Adder #(.width(1)) adder_2 (.a(XOR2_out), .b(A[1]), .out(adder_1_out[1]), .cin(adder_1_cout), .cout(adder_2_cout));
  Adder #(.width(1)) adder_3 (.a(XOR3_out), .b(A[2]), .out(adder_1_out[2]), .cin(adder_2_cout), .cout(adder_3_cout));
  Adder #(.width(1)) adder_4 (.a(XOR4_out), .b(A[3]), .out(adder_1_out[3]), .cin(adder_3_cout), .cout(adder_4_cout));
  xor XOR_2 (XOR_2_out, adder_3_cout, adder_4_cout);
  Multiplexer #(.select(3), .width(4), .enable("false")) multiplexer_1 (
    .in0(adder_1_out), .in1(adder_1_out), .in2(AND_out), .in3(OR_out), .in4(XOR_out), .in5({B[2:0], 1'b0}),
    .in6({1'b0, A[3:1]}), .out(OUTPUT), .sel({S2, S1, S0}));  // open: in7
  LED OVERFLOW (.in(XOR_2_out));
  or OR1 (OR1_out, OUTPUT[0], OUTPUT[1]);
  or OR2 (OR2_out, OUTPUT[2], OUTPUT[3]);
  or OR3 (OR3_out, OR1_out, OR2_out);
  not not_1 (not_1_out, OR3_out);
  LED ZERO_FLAG (.in(not_1_out));

  // Notes on the sheet:
  //   A
  //   B
  //   A
  //   B
  //   A
  //   B
  //   FOUR_BIT_ALU
  //   LEFT_SHIFT
  //   RIGHT_SHIFT
  //   CONSTATNT
  //   CONSTATNT
  //   FULL_ADDER
  //   FULL_ADDER
  //   FULL_ADDER
  //   FULL_ADDER
  //   MULTIPLEXER
  //   NOT_GATE
endmodule
